# Fritzing sketch Arduino MEGA (saved by Fritzing 0.9.9b)
breadboards: 1

parts:
  Компонент2 = Arduino Mega 2560 (Rev3)
  Компонент3 = Bluetooth HC-05 Macho
  A3 = GY-BMP280 Breakout
  A4 = DHT22 module
  Компонент4 = Temperature Sensor - LM75

nets:
  N1: Компонент2.D21/SCL, A3.Pin_3, Компонент4.SCL
  N2: Компонент2.D20/SDA, A3.Pin_4, Компонент4.SDA
  N3: Компонент2.D19/RX1, Компонент3.TXD
  N4: Компонент2.D18/TX1, Компонент3.RXD
  VCC: Компонент2.5V, Компонент3.VCC, A3.Pin_1, A4.+, Компонент4.Vcc
  GND: Компонент2.GND, Компонент3.GND, A3.Pin_2, A4.-, Компонент4.GND
  N5: Компонент2.D5_PWM, A4.Out

custom parts:
  DHT22 module: DHT22 module. Pins VCC Data GND.
  Temperature Sensor - LM75: Description: The LM75B and LM75C are industry-standard digital temperature semsors with integrated Sigma-Delta analog-to-digital converter and I2C interface. The LM75 provides 9-bit digital readings with an accuracy of +-2 Celcius degrees Features: No external Components required Shutdown mode to minimize power counsumption Up to Eight LM75s can be connected to a single bus Supply voltage: 3V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
